# Fritzing sketch schematic (saved by Fritzing 0.8.7b)
breadboards: 1

parts:
  Part1 = Thumb Joystick
  Part2 = Thumb Joystick
  Part3 = LED Matrix - Serial Interface - Red/Green/Blue
  J1 = Piezo Speaker
  Part4 = Arduino Uno (Rev3)
  Part5 = LED Matrix - Serial Interface - Red/Green/Blue
  Part6 = LED Matrix - Serial Interface - Red/Green/Blue
  Part7 = LED Matrix - Serial Interface - Red/Green/Blue

nets:
  GND: Part1.GND, Part2.GND, Part3.GND, J1.pin1, Part4.GND, Part5.GND, Part7.GND
  N1: Part1.SEL, Part4.D6_PWM
  N2: Part1.HORZ, Part4.A1
  N3: Part1.VERT, Part4.A0
  VCC: Part1.VCC, Part2.VCC, Part3.VCC, Part4.5V, Part5.VCC, Part7.VCC
  N4: Part2.SEL, Part4.D7
  N5: Part2.HORZ, Part4.A3
  N6: Part2.VERT, Part4.A2
  N7: Part3.SCK, Part4.D13/SCK, Part5.SCK, Part6.SCK, Part7.SCK
  N8: Part3.CS, Part4.D11_PWM/MOSI
  N9: Part3.MISO, Part4.D12/MISO, Part5.MISO, Part6.MISO, Part7.MISO
  N10: J1.pin2, Part4.D2
  N11: Part4.D8, Part5.CS
  N12: Part4.D9_PWM, Part7.CS
  N13: Part4.D10_PWM/SS, Part6.CS
